# Fritzing sketch Circuit_Diagram (saved by Fritzing 0.9.3b)
circuit board: 31.0485cm x 16.1025cm
breadboards: 2

parts:
  Arduino_MEGA_2560 = Arduino Mega 2560 (Rev3)
  Bluetooth_Module = Bluetooth HC-06d [package=THT]
  REAR_Ultrasonic_sensor = hc-sr04
  FRONT_ultrasonic_sensor = hc-sr04
  Micro_SD_card_reader = MicroSD Card Module
  LED_(Backward) = LED - 3mm [color="Red (660nm)" package="3 mm [THT]"]
  LED_(Forward) = LED - 3mm [color="Green (570nm)" package="3 mm [THT]"]
  LED_(Car_Going_Right) = LED - 3mm [color="Blue (470nm)" package="3 mm [THT]"]
  LED_(Car_Turning_Left) = LED - 3mm [color="Blue (470nm)" package="3 mm [THT]"]
  LED_(Car_Warns_of_obstacles) = LED - 3mm [color="Red (660nm)" package="3 mm [THT]"]

nets:
  N1: Arduino_MEGA_2560.A8, LED_(Backward).anode
  N2: Arduino_MEGA_2560.A9, LED_(Car_Warns_of_obstacles).anode
  N3: Arduino_MEGA_2560.A10, LED_(Car_Going_Right).anode
  N4: Arduino_MEGA_2560.A11, REAR_Ultrasonic_sensor.Trig, REAR_Ultrasonic_sensor.GND
  N5: Arduino_MEGA_2560.A12, REAR_Ultrasonic_sensor.Echo
  N6: Arduino_MEGA_2560.A13, FRONT_ultrasonic_sensor.Trig
  N7: Arduino_MEGA_2560.A14, FRONT_ultrasonic_sensor.Echo
  N8: Arduino_MEGA_2560.A5, LED_(Car_Turning_Left).anode
  N9: Arduino_MEGA_2560.A7, LED_(Forward).anode
  GND: Arduino_MEGA_2560.GND, Bluetooth_Module.GND, FRONT_ultrasonic_sensor.GND, Micro_SD_card_reader.GND
  3V3: Arduino_MEGA_2560.3V3, Bluetooth_Module.VCC
  VCC: Arduino_MEGA_2560.5V, REAR_Ultrasonic_sensor.VCC, FRONT_ultrasonic_sensor.VCC, Micro_SD_card_reader.VCC, LED_(Backward).cathode, LED_(Forward).cathode, LED_(Car_Going_Right).cathode, LED_(Car_Turning_Left).cathode, LED_(Car_Warns_of_obstacles).cathode
  N10: Arduino_MEGA_2560.D0_RX0, Bluetooth_Module.RXD
  N11: Arduino_MEGA_2560.D1_TX0, Bluetooth_Module.TXD
  N12: Arduino_MEGA_2560.D50, Micro_SD_card_reader.MISO
  N13: Arduino_MEGA_2560.D51, Micro_SD_card_reader.MOSI
  N14: Arduino_MEGA_2560.D52, Micro_SD_card_reader.SCK
  N15: Arduino_MEGA_2560.D53, Micro_SD_card_reader.CS

custom parts:
  Bluetooth HC-06d: Bluetooth HC-06 - face down, pins down 16.5mm x 37.5mm PCB
